# Fritzing sketch initial (saved by Fritzing 0.9.3b)
breadboards: 1

parts:
  A1 = Arduino UNO R4 WiFi
  U1 = L9110 H-bridge module [part_number="L9110 H-bridge"]
  U2 = L9110 H-bridge module [part_number="L9110 H-bridge"]
  M1 = DC Motor
  M2 = DC Motor
  M3 = DC Motor
  M4 = DC Motor

nets:
  VCC: A1.Pin_8, A1.Pin_27, U1.VCC, U2.VCC
  N1: A1.Pin_35, U1.A-IA
  N2: A1.Pin_36, U1.A-IB
  N3: A1.Pin_37, U1.B-IB
  N4: A1.Pin_38, U1.B-IA
  N5: A1.Pin_39, U2.A-IA
  N6: A1.Pin_40, U2.A-IB
  N7: A1.Pin_41, U2.B-IA
  N8: A1.Pin_42, U2.B-IB
  GND: A1.Pin_48, U1.GND, U2.GND
  N9: U1.MOTOR_A-A, M2.pin_2
  N10: U1.MOTOR_A-B, M2.pin_1
  N11: U1.MOTOR_B-A, M1.pin_2
  N12: U1.MOTOR_B-B, M1.pin_1
  N13: U2.MOTOR_A-A, M3.pin_2
  N14: U2.MOTOR_A-B, M3.pin_1
  N15: U2.MOTOR_B-A, M4.pin_2
  N16: U2.MOTOR_B-B, M4.pin_1

custom parts:
  Arduino UNO R4 WiFi: The Arduino UNO R4 WiFi merges the RA4M1 microprocessor from Renesas with the ESP32-S3 from Espressif, creating an all-in-one tool for makers with enhanced processing power and a diverse array of new peripherals.
