# Fritzing sketch register (saved by Fritzing 0.9.3b)
breadboards: 1

parts:
  U1 = 74HC595 [package="DIP16 [THT]"]
  A1 = Arduino UNO R4 WiFi

nets:
  N1: U1.GND, A1.Pin_9, A1.Pin_48
  N2: U1.MR, U1.VCC, A1.Pin_8
  N3: U1.SH_CP, A1.Pin_50
  N4: U1.ST_CP, A1.Pin_51
  N5: U1.OE, A1.Pin_15
  N6: U1.DS, A1.Pin_14

custom parts:
  Arduino UNO R4 WiFi: The Arduino UNO R4 WiFi merges the RA4M1 microprocessor from Renesas with the ESP32-S3 from Espressif, creating an all-in-one tool for makers with enhanced processing power and a diverse array of new peripherals.
