# Fritzing sketch newsonic (saved by Fritzing 0.9.3b)
breadboards: 1

parts:
  A1 = Arduino UNO R4 WiFi
  U1 = 74HC595 SMD [package="SO16 [SMD]"]
  U2 = 74HC595 SMD [package="SO16 [SMD]"]  # not connected
  hc-sr1 = hc-sr04
  hc-sr2 = hc-sr04
  hc-sr3 = hc-sr04
  hc-sr4 = hc-sr04

nets:
  N1: A1.Pin_8, A1.Pin_27, hc-sr2.GND
  N2: A1.Pin_16, hc-sr3.Trig
  N3: A1.Pin_17, hc-sr3.Echo
  N4: A1.Pin_35, hc-sr4.Trig
  N5: A1.Pin_36, hc-sr4.Echo
  N6: A1.Pin_37, hc-sr2.Trig
  N7: A1.Pin_38, hc-sr2.Echo
  N8: A1.Pin_46, hc-sr1.Trig
  N9: A1.Pin_47, hc-sr1.Echo
  GND: A1.Pin_48, hc-sr1.GND, hc-sr3.GND, hc-sr4.GND
  N10: U1.Q4, hc-sr1.VCC
  N11: U1.Q5, hc-sr4.VCC
  N12: U1.Q6, hc-sr3.VCC
  N13: U1.Q7, hc-sr2.VCC

custom parts:
  Arduino UNO R4 WiFi: The Arduino UNO R4 WiFi merges the RA4M1 microprocessor from Renesas with the ESP32-S3 from Espressif, creating an all-in-one tool for makers with enhanced processing power and a diverse array of new peripherals.
