# Fritzing sketch pwm (saved by Fritzing 0.9.3b)
breadboards: 1

parts:
  A1 = Arduino UNO R4 WiFi
  U1 = L9110 H-bridge module [part_number="L9110 H-bridge"]
  U2 = L9110 H-bridge module [part_number="L9110 H-bridge"]

nets:
  VCC: A1.Pin_8, A1.Pin_27, U1.VCC, U2.VCC
  GND: A1.Pin_18, A1.Pin_30, A1.Pin_48, U1.GND, U2.GND
  N1: A1.Pin_39, U1.B-IA, U1.A-IA
  N2: A1.Pin_40, U1.B-IB, U1.A-IB
  N3: A1.Pin_44, U2.B-IB, U2.A-IB
  N4: A1.Pin_45, U2.B-IA, U2.A-IA

custom parts:
  Arduino UNO R4 WiFi: The Arduino UNO R4 WiFi merges the RA4M1 microprocessor from Renesas with the ESP32-S3 from Espressif, creating an all-in-one tool for makers with enhanced processing power and a diverse array of new peripherals.
