# Fritzing sketch steps (saved by Fritzing 0.9.3b)
breadboards: 1

parts:
  Εξάρτημα1 = FC-03
  A1 = Arduino UNO R4 WiFi
  Εξάρτημα2 = FC-03
  Εξάρτημα3 = FC-03
  Εξάρτημα4 = FC-03
  U1 = 74HC595 SMD [package="SO16 [SMD]"]
  U2 = 74HC595 SMD [package="SO16 [SMD]"]  # not connected

nets:
  N1: Εξάρτημα1.VCC, U1.Q0
  GND: Εξάρτημα1.GND, A1.Pin_2, A1.Pin_9, Εξάρτημα2.GND, Εξάρτημα3.GND, Εξάρτημα4.GND
  N2: Εξάρτημα1.A0, A1.Pin_12
  N3: A1.Pin_13, Εξάρτημα2.A0
  N4: A1.Pin_14, Εξάρτημα4.A0
  N5: A1.Pin_15, Εξάρτημα3.A0
  N6: Εξάρτημα2.VCC, U1.Q2
  N7: Εξάρτημα3.VCC, U1.Q3
  N8: Εξάρτημα4.VCC, U1.Q4

custom parts:
  FC-03: FC-03, LM393 IR Speed Sensor Encoder By Nandan
  Arduino UNO R4 WiFi: The Arduino UNO R4 WiFi merges the RA4M1 microprocessor from Renesas with the ESP32-S3 from Espressif, creating an all-in-one tool for makers with enhanced processing power and a diverse array of new peripherals.
